// Digital circuit soc.dig as structural Verilog
module soc (
  input  [31:0] instr
);

  wire advance_out;
  wire [4:0] dec2_1_rd, dec2_1_rs1, dec2_1_rs2;
  wire [9:0] dec2_1_funct;
  wire [31:0] alu_1_result, dec2_1_op1, dec2_1_op2, register_file_1_d_rs1, register_file_1_d_rs2;

  Button advance (.out(advance_out));
  dec2 dec2_1 (
    .opcode(instr[6:0]), .instr(instr), .val_rs1(register_file_1_d_rs1), .val_rs2(register_file_1_d_rs2),
    .rs1(dec2_1_rs1), .rs2(dec2_1_rs2), .rd(dec2_1_rd), .op1(dec2_1_op1), .op2(dec2_1_op2),
    .funct(dec2_1_funct));
  alu alu_1 (.op1(dec2_1_op1), .op2(dec2_1_op2), .funct(dec2_1_funct), .result(alu_1_result));
  register_file register_file_1 (
    .rs1(dec2_1_rs1), .rs2(dec2_1_rs2), .rd(dec2_1_rd), .D_in(alu_1_result), .clock(advance_out),
    .D_rs1(register_file_1_d_rs1), .D_rs2(register_file_1_d_rs2));
endmodule
