// Digital circuit decoder.dig as structural Verilog
module decoder (
  input  [31:0] D,
  output [1:0] rs,
  output [1:0] rd,
  output add,
  output [15:0] value,
  output jump
);

  Decoder #(.Selector_Bits(3)) decoder_1 (
    .sel(D[26:24]), .out_0(add), .out_7(jump));  // open: out_1, out_2, out_3, out_4, out_5, out_6

  assign rd = D[17:16];
  assign rs = D[21:20];
  assign value = D[15:0];

  // Notes on the sheet:
  //   D: Take 32-bits input
endmodule
