// Digital circuit front.dig as structural Verilog
module front (
  input  [15:0] value,
  input  [1:0] dest,
  input  [1:0] src,
  output [15:0] R0,
  output [15:0] R1,
  output [15:0] R2,
  output [15:0] R3,
  output [1:0] rs,
  output [15:0] A,
  output [15:0] B,
  output [1:0] rd,
  output [3:0] pc,
  output [15:0] A_2,
  output [15:0] B_2
);

  wire add, add_out, advance_out, asm_1_store_clk, jmp_out, jump, mode_out, pmshim_1_c, pmshim_1_ld,
       pmshim_1_str;
  wire [3:0] pmshim_1_a;
  wire [15:0] execute_1_sum;
  wire [31:0] asm_1_inst, fetch16_1_d_inst, pmshim_1_d_in, Program_d;

  LED programming (.in(mode_out));
  DipSwitch mode (.out(mode_out));
  Button u_add (.out(add_out));
  Button jmp (.out(jmp_out));
  asm asm_1 (
    .mode(mode_out), .imm(value), .dest(dest), .src(src), .add(add_out), .jump(jmp_out),
    .store_clk(asm_1_store_clk), .inst(asm_1_inst));
  pmshim pmshim_1 (
    .pc(pc), .S_C(asm_1_store_clk), .inst(asm_1_inst), .A(pmshim_1_a), .D_in(pmshim_1_d_in),
    .str(pmshim_1_str), .C(pmshim_1_c), .ld(pmshim_1_ld));
  EEPROMDualPort #(.AddrBits(4), .Bits(32)) Program (
    .A(pmshim_1_a), .Din(pmshim_1_d_in), .str(pmshim_1_str), .C(pmshim_1_c), .ld(pmshim_1_ld), .D(Program_d));
  Button advance (.out(advance_out));
  LED add_2 (.in(add));
  LED u_jump (.in(jump));
  fetch16 fetch16_1 (
    .mode(mode_out), .D_stored(Program_d), .D_bypass(asm_1_inst), .C(advance_out), .value(A), .jump(jump),
    .pc(pc), .D_inst(fetch16_1_d_inst));
  decoder decoder_1 (.D(fetch16_1_d_inst), .rs(rs), .rd(rd), .add(add), .value(A), .jump(jump));
  execute execute_1 (.add(add), .value(A), .b(B), .sum(execute_1_sum));
  regfile regfile_1 (.rs(rs), .rd(rd), .D(execute_1_sum), .CL(advance_out), .R0(R0), .R1(R1), .R2(R2), .R3(R3), .B(B));

  assign A_2 = A;
  assign B_2 = B;

  // Notes on the sheet:
  //   contents of Program (hex, n*v repeats v):
  //   64,100c8,120063,230022,30002a,7000001
endmodule
